# Fritzing sketch BlueTooth_Display_Teil_4 (saved by Fritzing 0.9.3b)
breadboards: 1

parts:
  R1 = Trimmer Potentiometer [maximum_resistance=10kΩ package=THT]
  HD44780_2004_LCD_Display_4x20_characters_Green1 = HD44780 2004 LCD Display 4x20 characters Green
  Uno_R3_Board_with_ATmega328P1 = Uno R3 Board with ATmega328P
  R2 = Resistor [tolerance=±5% resistance=130 package=THT]
  Bauteil1 = Bluetooth HC-05 Macho  # not connected
  Bauteil2 = IFR520 MOS module [package=THT]
  KY-004_Button_Module1 = KY-004 Button Module

nets:
  GND: R1.leg1, HD44780_2004_LCD_Display_4x20_characters_Green1.VSS, HD44780_2004_LCD_Display_4x20_characters_Green1.R/W, Uno_R3_Board_with_ATmega328P1.GND, Bauteil2.GND, KY-004_Button_Module1.-
  N1: R1.wiper, HD44780_2004_LCD_Display_4x20_characters_Green1.V0
  VDD: R1.leg2, HD44780_2004_LCD_Display_4x20_characters_Green1.VDD, Uno_R3_Board_with_ATmega328P1.A5/SCL, Uno_R3_Board_with_ATmega328P1.5V, R2.Pin_1, Bauteil2.VCC
  N2: HD44780_2004_LCD_Display_4x20_characters_Green1.RS, Uno_R3_Board_with_ATmega328P1.D8
  N3: HD44780_2004_LCD_Display_4x20_characters_Green1.E, Uno_R3_Board_with_ATmega328P1.D13/SCK
  N4: HD44780_2004_LCD_Display_4x20_characters_Green1.DB4, Uno_R3_Board_with_ATmega328P1.D12/MISO
  N5: HD44780_2004_LCD_Display_4x20_characters_Green1.DB5, Uno_R3_Board_with_ATmega328P1.D11_PWM/MOSI
  N6: HD44780_2004_LCD_Display_4x20_characters_Green1.DB6, Uno_R3_Board_with_ATmega328P1.D10_PWM/SS
  N7: HD44780_2004_LCD_Display_4x20_characters_Green1.DB7, Uno_R3_Board_with_ATmega328P1.D9_PWM
  N8: HD44780_2004_LCD_Display_4x20_characters_Green1.LED_A, R2.Pin_0
  N9: HD44780_2004_LCD_Display_4x20_characters_Green1.LED_K, Bauteil2.V-
  N10: Uno_R3_Board_with_ATmega328P1.D2, KY-004_Button_Module1.S
  N11: Uno_R3_Board_with_ATmega328P1.D5_PWM, Bauteil2.SIG

custom parts:
  HD44780 2004 LCD Display 4x20 characters Green: This 20x4 LCD module with a built-in HD44780 Controller allows for the display of 20x4 characters in black font on a green background. The control of the display, for example, via an Arduino, Raspberry Pi, etc., the connection of The Display can be made directly to the GPIO Ports of the Arduino. The assignment of the 16 contacts looks like the following: VSS: GND (ground VDD: +5V supply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
  Uno R3 Board with ATmega328P: The right Board for all - no matter whether you are a beginner or a professional, with simple programming via a USB cable and the solderless plug-in pins anyone can Tinker within minutes of the first project! By 14 digital in - and outputs and 6 analog inputs of the UNO R3 can be used for larger projects! Thanks to the ATmega328P micro-controller, as well as more sophisticated programs to be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
  KY-004 Button Module: Universal Button Module for direct use with Arduino, Raspberry & Co. Operating Voltage 3.3 V - 5 V Usual high quality and fast delivery directly from Germany by order AZ Delivery Of course, you will receive when you purchase through AZDelivery fully automatically and guarantees a Invoice incl. VAT and according to German Standards Guaranteed ROHS compliance by purchase from the German trader
